// Logisim project logisim-computer.circ as structural Verilog: 1 circuit, main circuit main
module main (
  input  in_1,
  input  in_2,
  input  in_3,
  input  in_4,
  input  in_5,
  input  in_6,
  input  in_7,
  input  in_8,
  input  in_9,
  input  in_10,
  input  in_11,
  input  in_12,
  input  in_13,
  input  in_14,
  input  in_15
);

  wire AI, AO, BI, BO, buffer_1_out, CE, CLK, clock_1_out, CLR, CO, decoder_1_out0, decoder_1_out1,
       decoder_1_out2, decoder_1_out3, decoder_1_out4, decoder_1_out5, decoder_1_out6, decoder_1_out7, II,
       IO, J, MAI, MI, MO, not_1_out, OI, or_1_out, Override_out, SO, SS, xor_3_out;
  wire [2:0] counter_2_q, subtractor_1_out;
  wire [3:0] bit_extender_1_out, bit_extender_2_out, controlled_buffer_4_out, MA, PC;
  wire [7:0] adder_1_out, AR, bit_extender_3_out, bit_extender_4_out, bit_extender_5_out, BR, Bus,
       controlled_buffer_1_out, controlled_buffer_2_out, controlled_buffer_3_out, controlled_buffer_8_out,
       controlled_buffer_9_out, controlled_buffer_10_out, IR, ram_1_data, register_5_q, xor_2_out;
  wire [15:15] rom_1_data;

  Bit_Extender #(.out_width(4)) bit_extender_1 (.in(controlled_buffer_1_out), .out(bit_extender_1_out));
  assign controlled_buffer_1_out = J ? Bus : 8'bz;  // Controlled_Buffer controlled_buffer_1
  Bit_Extender #(.out_width(4)) bit_extender_2 (.in(Bus), .out(bit_extender_2_out));
  assign controlled_buffer_2_out = MI ? Bus : 8'bz;  // Controlled_Buffer controlled_buffer_2
  assign controlled_buffer_3_out = II ? Bus : 8'bz;  // Controlled_Buffer controlled_buffer_3
  Clock clock_1 (.out(clock_1_out));
  xor xor_1 (CLK, clock_1_out, Override_out);
  Button Override (.out(Override_out));
  Counter #(.width(4), .max('hf)) counter_1 (
    .load(J), .D(bit_extender_1_out), .count(CE), .Q(PC), .clk(CLK), .clr(CLR));  // open: carry
  Register #(.width(4)) register_1 (.D(controlled_buffer_4_out), .Q(MA), .clk(CLK), .clr(CLR));  // open: en
  assign controlled_buffer_4_out = MAI ? bit_extender_2_out : 4'bz;  // Controlled_Buffer controlled_buffer_4
  Register register_2 (.D(controlled_buffer_3_out), .Q(IR), .clk(CLK), .clr(CLR));  // open: en
  assign Bus = CO ? bit_extender_3_out : 8'bz;  // Controlled_Buffer controlled_buffer_5
  assign bit_extender_3_out = {{4{1'b0}}, PC};  // Bit_Extender bit_extender_3
  RAM #(.addrWidth(4), .bus("separate")) ram_1 (
    .addr(MA), .din(controlled_buffer_2_out), .data(ram_1_data), .str(MI), .clk(CLK), .ld(MO));  // open: sel, clr
  assign Bus = MO ? ram_1_data : 8'bz;  // Controlled_Buffer controlled_buffer_6
  assign bit_extender_4_out = {{4{1'b0}}, IR[7:4]};  // Bit_Extender bit_extender_4
  assign Bus = IO ? bit_extender_4_out : 8'bz;  // Controlled_Buffer controlled_buffer_7
  assign bit_extender_5_out = {{7{SS}}, SS};  // Bit_Extender bit_extender_5
  assign controlled_buffer_8_out = AI ? Bus : 8'bz;  // Controlled_Buffer controlled_buffer_8
  assign controlled_buffer_9_out = BI ? Bus : 8'bz;  // Controlled_Buffer controlled_buffer_9
  assign controlled_buffer_10_out = OI ? Bus : 8'bz;  // Controlled_Buffer controlled_buffer_10
  assign xor_2_out = BR ^ bit_extender_5_out;  // XOR_Gate xor_2, 8 bits wide
  Register register_3 (.D(controlled_buffer_8_out), .Q(AR), .clk(CLK), .clr(CLR));  // open: en
  Register register_4 (.D(controlled_buffer_9_out), .Q(BR), .clk(CLK), .clr(CLR));  // open: en
  Register register_5 (.D(controlled_buffer_10_out), .Q(register_5_q), .clk(CLK), .clr(CLR));  // open: en
  assign Bus = SO ? adder_1_out : 8'bz;  // Controlled_Buffer controlled_buffer_11
  Adder adder_1 (.a(AR), .b(xor_2_out), .out(adder_1_out), .cin(SS));  // open: cout
  assign Bus = AO ? AR : 8'bz;  // Controlled_Buffer controlled_buffer_12
  assign Bus = BO ? BR : 8'bz;  // Controlled_Buffer controlled_buffer_13
  Hex_Digit_Display hex_digit_display_1 (.value(register_5_q[7:4]));  // open: dp
  Hex_Digit_Display hex_digit_display_2 (.value(register_5_q[3:0]));  // open: dp
  Counter #(.width(3), .max('h7)) counter_2 (
    .load(1'b0), .count(1'b1), .Q(counter_2_q), .clk(not_1_out), .clr(buffer_1_out));  // open: D, carry
  not not_1 (not_1_out, CLK);
  buf buffer_1 (buffer_1_out, CLR);
  Pull_Resistor pull_resistor_1 (.node(buffer_1_out));
  or or_1 (or_1_out, decoder_1_out3, decoder_1_out4, decoder_1_out5, decoder_1_out6, decoder_1_out7);
  Decoder #(.select(3), .disabled(0)) decoder_1 (
    .out0(decoder_1_out0), .out1(decoder_1_out1), .out2(decoder_1_out2), .out3(decoder_1_out3),
    .out4(decoder_1_out4), .out5(decoder_1_out5), .out6(decoder_1_out6), .out7(decoder_1_out7),
    .sel(counter_2_q));  // open: en
  Subtractor #(.width(3)) subtractor_1 (.a(counter_2_q), .b(3'b011), .out(subtractor_1_out));  // open: bin, bout
  xor xor_3 (xor_3_out, CLR, or_1_out);
  assign buffer_1_out = xor_3_out ? rom_1_data[15] : 1'bz;  // Controlled_Buffer controlled_buffer_14
  buf buffer_2 (CO, decoder_1_out0);
  buf buffer_3 (MAI, decoder_1_out0);
  buf buffer_4 (MO, decoder_1_out1);
  buf buffer_5 (II, decoder_1_out1);
  buf buffer_6 (CE, decoder_1_out2);
  ROM #(.addrWidth(7), .dataWidth(16)) rom_1 (
    .addr({IR[3:0], subtractor_1_out}),
    .data({rom_1_data[15], OI, BO, BI, AO, AI, IO, II, SS, SO, MO, MI, MAI, CE, CO, J}), .sel(or_1_out));
  LED led_1 (.in(J));
  LED led_2 (.in(CO));
  LED led_3 (.in(CE));
  LED led_4 (.in(MAI));
  LED led_5 (.in(MI));
  LED led_6 (.in(MO));
  LED led_7 (.in(SO));
  LED led_8 (.in(SS));
  LED led_9 (.in(II));
  LED led_10 (.in(IO));
  LED led_11 (.in(AI));
  LED led_12 (.in(AO));
  LED led_13 (.in(BI));
  LED led_14 (.in(BO));
  LED led_15 (.in(OI));
  // Probe on Bus
  // Probe on PC
  // Probe on MA
  // Probe on IR
  // Probe on AR
  // Probe on BR
  Button button_1 (.out(CLR));
  buf buffer_7 (J, in_1);
  buf buffer_8 (CO, in_2);
  buf buffer_9 (CE, in_3);
  buf buffer_10 (MAI, in_4);
  buf buffer_11 (MI, in_5);
  buf buffer_12 (MO, in_6);
  buf buffer_13 (SO, in_7);
  buf buffer_14 (SS, in_8);
  buf buffer_15 (II, in_9);
  buf buffer_16 (IO, in_10);
  buf buffer_17 (AI, in_11);
  buf buffer_18 (AO, in_12);
  buf buffer_19 (BI, in_13);
  buf buffer_20 (BO, in_14);
  buf buffer_21 (OI, in_15);
  Pull_Resistor pull_resistor_2 (.node(J));
  Pull_Resistor pull_resistor_3 (.node(CO));
  Pull_Resistor pull_resistor_4 (.node(CE));
  Pull_Resistor pull_resistor_5 (.node(MAI));
  Pull_Resistor pull_resistor_6 (.node(MI));
  Pull_Resistor pull_resistor_7 (.node(MO));
  Pull_Resistor pull_resistor_8 (.node(SO));
  Pull_Resistor pull_resistor_9 (.node(SS));
  Pull_Resistor pull_resistor_10 (.node(II));
  Pull_Resistor pull_resistor_11 (.node(IO));
  Pull_Resistor pull_resistor_12 (.node(AI));
  Pull_Resistor pull_resistor_13 (.node(AO));
  Pull_Resistor pull_resistor_14 (.node(BI));
  Pull_Resistor pull_resistor_15 (.node(BO));
  Pull_Resistor pull_resistor_16 (.node(OI));

  // Notes on the sheet:
  //   Clock
  //   Program Counter
  //   Memory Address Register
  //   Memory
  //   Instruction Register
  //   ALU
  //   A Register
  //   B Register
  //   Output
  //   Micro Instruction Counter
  //   buffer_1 drives only 1 and floats otherwise
  //   Control Logic
  //   Goto Next Instruction
  //   buffer_2 drives only 1 and floats otherwise
  //   buffer_3 drives only 1 and floats otherwise
  //   buffer_4 drives only 1 and floats otherwise
  //   buffer_5 drives only 1 and floats otherwise
  //   buffer_6 drives only 1 and floats otherwise
  //   contents of rom_1 (hex, n*v repeats v):
  //   208 4020 8000 5*0 208 420 8000 5*0 208 810 8000 5*0 208 1020 440 8000 4*0 201 8000 6*0 208 1020 4c0
  //   8000 4*0 1800 8000 6*0 2400 8000 6*0 8000 7*0 8000 7*0 8000 7*0 8000 7*0 8000 7*0 8000 7*0 8000 7*0
  //   8000
  //   Control Flags
  //   buffer_7 drives only 1 and floats otherwise
  //   buffer_8 drives only 1 and floats otherwise
  //   buffer_9 drives only 1 and floats otherwise
  //   buffer_10 drives only 1 and floats otherwise
  //   buffer_11 drives only 1 and floats otherwise
  //   buffer_12 drives only 1 and floats otherwise
  //   buffer_13 drives only 1 and floats otherwise
  //   buffer_14 drives only 1 and floats otherwise
  //   buffer_15 drives only 1 and floats otherwise
  //   buffer_16 drives only 1 and floats otherwise
  //   buffer_17 drives only 1 and floats otherwise
  //   buffer_18 drives only 1 and floats otherwise
  //   buffer_19 drives only 1 and floats otherwise
  //   buffer_20 drives only 1 and floats otherwise
  //   buffer_21 drives only 1 and floats otherwise
endmodule
